# Fritzing sketch Node mcu with hc-sr04 (saved by Fritzing 0.9.3b)
breadboards: 1

parts:
  U1 = NodeMCU V1.0
  hc-sr1 = hc-sr04
  Part1 = Power Cell LiPo Charger/Booster
  Squix1 = OLED 0.96" 128x64 I2C SSD1306
  Part2 = Adafruit MicroSD card breakout board [part_number="Adafruit #254"]

nets:
  N1: U1.D1, hc-sr1.Trig
  N2: U1.D2, hc-sr1.Echo
  N3: U1.D3, Squix1.SCL
  N4: U1.D4, Squix1.SCA
  3V3: U1.3V3, Squix1.VCC, Part2.+3V3
  GND: U1.GND, hc-sr1.GND, Part1.GND, Squix1.GND, Part2.GND
  N5: U1.D5, Part2.CLK
  N6: U1.D6, Part2.DO
  N7: U1.D7, Part2.DI
  N8: U1.D8, Part2.CS
  VIN: U1.Vin, hc-sr1.VCC, Part1.5VIN

custom parts:
  NodeMCU V1.0: ESP8266 based NodeMCU
  Adafruit MicroSD card breakout board: Not just a simple breakout board, this microSD adapter goes the extra mile - designed for ease of use. Onboard 5v->3v regulator provides 150mA for power-hungry cards 3v level shifting means you can use this with ease on either 3v or 5v systems Uses a proper level shifting chip, not resistors: less problems, and faster read/write access Use 3 or 4 digital pins to read and write 2Gb+ of storage!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
